# Fritzing sketch Arduino Relay (saved by Fritzing 0.9.2b)
breadboards: 2

parts:
  U1 = 2-Channel 5v Relay Shield [package=relay-2ch5v10a]
  U2 = NodeMCU V1.0
  LED1 = smd LED [color="Red (633nm)" package="0603 [SMD]"]
  LED2 = LEDs [package=led10mm]
  R1 = Resistor [tolerance=±5% resistance=220 package="0402 [SMD]"]  # not connected
  R2 = Resistor [tolerance=±5% resistance=220 package="0805 [SMD]"]
  R3 = Resistor [tolerance=±5% resistance=220 package="0805 [SMD]"]

nets:
  N1: U1.VCC, U2.RSV#40
  GND: U1.GND, U1.JD-GND, U2.GND, LED1.cathode
  N2: U1.IN2, U2.D4
  N3: U1.K2-In, U2.3V3
  N4: U1.K2-Off, R2.Pin_1
  N5: U1.K2-On, R3.Pin_0
  N6: U2.CMD, LED2.C
  N7: LED2.A, R3.Pin_1

custom parts:
  2-Channel 5v Relay Shield: 2 Channel 5v Relay Shield w. 2x SPD-06VDC-SD-C
  NodeMCU V1.0: ESP8266 based NodeMCU
